# Fritzing sketch abajo joymax (saved by Fritzing 0.9.3b)
circuit board: 20cm x 20cm
breadboards: 1

parts:
  s1 = female pin header, 6 pins [form="♀ (female)"]
  R31 = Photocell (LDR) [package=THT]
  R32 = Photocell (LDR) [package=THT]
  R33 = Photocell (LDR) [package=THT]
  R34 = Photocell (LDR) [package=THT]
  R35 = Photocell (LDR) [package=THT]
  R36 = Photocell (LDR) [package=THT]
  R37 = Photocell (LDR) [package=THT]
  R38 = Photocell (LDR) [package=THT]
  R39 = Photocell (LDR) [package=THT]
  R40 = Photocell (LDR) [package=THT]
  R41 = Photocell (LDR) [package=THT]
  R42 = Photocell (LDR) [package=THT]
  R43 = Resistor [tolerance=±5% resistance=220 package=THT]
  R44 = Resistor [tolerance=±5% resistance=220 package=THT]
  R45 = Resistor [tolerance=±5% resistance=220 package=THT]
  R46 = Resistor [tolerance=±5% resistance=220 package=THT]
  R47 = Resistor [tolerance=±5% resistance=220 package=THT]
  R48 = Resistor [tolerance=±5% resistance=220 package=THT]
  R49 = Resistor [tolerance=±5% resistance=220 package=THT]
  R50 = Resistor [tolerance=±5% resistance=220 package=THT]
  R51 = Resistor [tolerance=±5% resistance=220 package=THT]
  R52 = Resistor [tolerance=±5% resistance=220 package=THT]
  R53 = Resistor [tolerance=±5% resistance=220 package=THT]
  R54 = Resistor [tolerance=±5% resistance=220 package=THT]
  RGB_SMD_LED12 = SMD RGB LED (WS2812) [package=5050]
  RGB_SMD_LED13 = SMD RGB LED (WS2812) [package=5050]
  RGB_SMD_LED14 = SMD RGB LED (WS2812) [package=5050]
  RGB_SMD_LED15 = SMD RGB LED (WS2812) [package=5050]
  RGB_SMD_LED16 = SMD RGB LED (WS2812) [package=5050]
  RGB_SMD_LED17 = SMD RGB LED (WS2812) [package=5050]
  RGB_SMD_LED18 = SMD RGB LED (WS2812) [package=5050]
  RGB_SMD_LED19 = SMD RGB LED (WS2812) [package=5050]
  RGB_SMD_LED20 = SMD RGB LED (WS2812) [package=5050]
  RGB_SMD_LED21 = SMD RGB LED (WS2812) [package=5050]
  U2 = ESP32S-HiLetgo [part_number=ESP32S-HiLetgo]
  J91 = Screw terminal - 2 pins [package=THT]
  PUENTE_H1 = CJMCU - 7960 [package=THT]
  PUENTE_H2 = CJMCU - 7960 [package=THT]
  PUENTE_H3 = CJMCU - 7960 [package=THT]
  PUENTE_H4 = CJMCU - 7960 [package=THT]
  R55 = Resistor [tolerance=±5% resistance=220 package=THT]
  J87 = Screw terminal - 2 pins [package=THT]
  J86 = Screw terminal - 2 pins [package=THT]
  J82 = Screw terminal - 2 pins [package=THT]
  J81 = Screw terminal - 2 pins [package=THT]

nets:
  VCC: s1.pin2, R31.pin_1, R32.pin_1, R33.pin_1, R34.pin_1, R35.pin_1, R36.pin_0, R37.pin_0, R38.pin_0, R39.pin_0, R40.pin_0, R41.pin_0, R42.pin_0, RGB_SMD_LED12.DOut, RGB_SMD_LED12.DIn, RGB_SMD_LED12.VCC, RGB_SMD_LED13.DOut, RGB_SMD_LED13.DIn, RGB_SMD_LED13.VCC, RGB_SMD_LED14.NC, RGB_SMD_LED14.VDD, RGB_SMD_LED14.VSS, RGB_SMD_LED15.NC, RGB_SMD_LED15.VDD, RGB_SMD_LED15.VSS, RGB_SMD_LED16.NC, RGB_SMD_LED16.VDD, RGB_SMD_LED16.VSS, RGB_SMD_LED17.NC, RGB_SMD_LED17.VDD, RGB_SMD_LED17.VSS, RGB_SMD_LED18.NC, RGB_SMD_LED18.VDD, RGB_SMD_LED18.VSS, RGB_SMD_LED19.DOut, RGB_SMD_LED19.DIn, RGB_SMD_LED19.VCC, RGB_SMD_LED20.DOut, RGB_SMD_LED20.DIn, RGB_SMD_LED20.VCC, RGB_SMD_LED21.DOut, RGB_SMD_LED21.DIn, RGB_SMD_LED21.VCC, PUENTE_H1.VCC, PUENTE_H1.EN1, PUENTE_H1.EN2, PUENTE_H2.VCC, PUENTE_H2.EN1, PUENTE_H2.EN2, PUENTE_H3.VCC, PUENTE_H3.EN1, PUENTE_H3.EN2, PUENTE_H4.VCC, PUENTE_H4.EN1, PUENTE_H4.EN2
  N1: s1.pin3, R43.Pin_0, R44.Pin_0, R45.Pin_0, R46.Pin_0, R47.Pin_1, R48.Pin_0, R49.Pin_0, R50.Pin_0, R51.Pin_0, R52.Pin_0, R53.Pin_1, R54.Pin_0, U2.GND, PUENTE_H1.GND#0, PUENTE_H2.GND#0, PUENTE_H3.GND#0, PUENTE_H4.GND#0, R55.Pin_1
  N2: s1.pin4, U2.VIN
  N3: s1.pin5, U2.GPIO22
  N4: s1.pin6, U2.GPIO21
  N5: R31.pin_0, R43.Pin_1, U2.GPIO36
  N6: R32.pin_0, R46.Pin_1
  N7: R33.pin_0, R45.Pin_1, U2.GPIO4
  N8: R34.pin_0, R44.Pin_1, U2.GPIO0
  N9: R35.pin_0, R47.Pin_0, U2.GPIO2
  N10: R36.pin_1, R53.Pin_0, U2.GPIO39
  N11: R37.pin_1, R48.Pin_1, U2.GPIO15
  N12: R38.pin_1, R49.Pin_1, U2.GPIO25
  N13: R39.pin_1, R50.Pin_1, U2.GPIO33
  N14: R40.pin_1, R51.Pin_1, U2.GPIO32
  N15: R41.pin_1, R54.Pin_1, U2.GPIO34
  N16: R42.pin_1, R52.Pin_1, U2.GPIO35
  VDD: RGB_SMD_LED12.NC, RGB_SMD_LED12.VDD, RGB_SMD_LED12.VSS, RGB_SMD_LED13.NC, RGB_SMD_LED13.VDD, RGB_SMD_LED13.VSS, RGB_SMD_LED14.DOut, RGB_SMD_LED14.DIn, RGB_SMD_LED14.VCC, RGB_SMD_LED15.DOut, RGB_SMD_LED15.DIn, RGB_SMD_LED15.VCC, RGB_SMD_LED16.DOut, RGB_SMD_LED16.DIn, RGB_SMD_LED16.VCC, RGB_SMD_LED17.DOut, RGB_SMD_LED17.DIn, RGB_SMD_LED17.VCC, RGB_SMD_LED18.DOut, RGB_SMD_LED18.DIn, RGB_SMD_LED18.VCC, RGB_SMD_LED19.NC, RGB_SMD_LED19.VDD, RGB_SMD_LED19.VSS, RGB_SMD_LED20.NC, RGB_SMD_LED20.VDD, RGB_SMD_LED20.VSS, RGB_SMD_LED21.NC, RGB_SMD_LED21.VDD, RGB_SMD_LED21.VSS, R55.Pin_0
  N17: U2.GPIO26, PUENTE_H2.PWM1
  N18: U2.GPIO27, PUENTE_H2.PWM2
  N19: U2.GPIO14, PUENTE_H1.PWM1
  N20: U2.GPIO12, PUENTE_H1.PWM2
  N21: U2.GPIO17, PUENTE_H4.PWM1
  N22: U2.GPIO5, PUENTE_H4.PWM2
  N23: U2.GPIO18, PUENTE_H3.PWM1
  N24: U2.GPIO19, PUENTE_H3.PWM2
  N25: J91.pin1, PUENTE_H1.VS, PUENTE_H2.VS, PUENTE_H3.VS, PUENTE_H4.VS
  N26: J91.pin2, PUENTE_H1.GND#11, PUENTE_H2.GND#11, PUENTE_H3.GND#11, PUENTE_H4.GND#11
  N27: PUENTE_H1.OUT1, J87.pin1
  N28: PUENTE_H1.OUT2, J87.pin2
  N29: PUENTE_H2.OUT1, J86.pin1
  N30: PUENTE_H2.OUT2, J86.pin2
  N31: PUENTE_H3.OUT1, J82.pin1
  N32: PUENTE_H3.OUT2, J82.pin2
  N33: PUENTE_H4.OUT1, J81.pin1
  N34: PUENTE_H4.OUT2, J81.pin2

notes:
  VM
  GND
  vin
  SCL
  3.3v
  SDA
  GREGORIANOS

custom parts:
  ESP32S-HiLetgo: HiLetgo ESP-WROOM-32 ESP32 ESP-32S Development Board 2.4GHz Dual-Mode WiFi + Bluetooth Dual Cores Microcontroller The ESP32 integrated with Antenna switches, RF Balun, power amplifiers, low-noise amplifiers, filters, and management modules, and the entire solution occupies the least area of PCB. 2.4 GHz Wi-Fi plus Bluetooth dual-mode chip, with TSMC Ultra-low power consumption 40nm technology,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
  CJMCU - 7960: DRIVER
