# Fritzing sketch abajo azul (saved by Fritzing 0.9.3b)
circuit board: 20cm x 20cm
breadboards: 1

parts:
  R1 = Photocell (LDR) [package=THT]
  R2 = Resistor [tolerance=±5% resistance=220 package=THT]
  R3 = Photocell (LDR) [package=THT]
  R5 = Photocell (LDR) [package=THT]
  R6 = Photocell (LDR) [package=THT]
  R8 = Photocell (LDR) [package=THT]
  R9 = Photocell (LDR) [package=THT]
  R10 = Photocell (LDR) [package=THT]
  R11 = Photocell (LDR) [package=THT]
  R12 = Photocell (LDR) [package=THT]
  R13 = Photocell (LDR) [package=THT]
  R14 = Photocell (LDR) [package=THT]
  R15 = Photocell (LDR) [package=THT]
  R18 = Resistor [tolerance=±5% resistance=220 package=THT]
  R19 = Resistor [tolerance=±5% resistance=220 package=THT]
  R20 = Resistor [tolerance=±5% resistance=220 package=THT]
  R21 = Resistor [tolerance=±5% resistance=220 package=THT]
  R22 = Resistor [tolerance=±5% resistance=220 package=THT]
  R23 = Resistor [tolerance=±5% resistance=220 package=THT]
  R24 = Resistor [tolerance=±5% resistance=220 package=THT]
  R26 = Resistor [tolerance=±5% resistance=220 package=THT]
  R27 = Resistor [tolerance=±5% resistance=220 package=THT]
  R28 = Resistor [tolerance=±5% resistance=220 package=THT]
  R29 = Resistor [tolerance=±5% resistance=220 package=THT]
  RGB_SMD_LED4 = SMD RGB LED (WS2812) [package=5050]
  RGB_SMD_LED6 = SMD RGB LED (WS2812) [package=5050]
  RGB_SMD_LED5 = SMD RGB LED (WS2812) [package=5050]
  RGB_SMD_LED1 = SMD RGB LED (WS2812) [package=5050]
  RGB_SMD_LED9 = SMD RGB LED (WS2812) [package=5050]
  RGB_SMD_LED10 = SMD RGB LED (WS2812) [package=5050]
  RGB_SMD_LED7 = SMD RGB LED (WS2812) [package=5050]
  RGB_SMD_LED11 = SMD RGB LED (WS2812) [package=5050]
  RGB_SMD_LED2 = SMD RGB LED (WS2812) [package=5050]
  RGB_SMD_LED3 = SMD RGB LED (WS2812) [package=5050]
  U1 = ESP32S-HiLetgo [part_number=ESP32S-HiLetgo]
  J62 = female pin header, 2 pins [form="♀ (female)"]
  Componente4 = Motor Driver 1A Dual TB6612FNG
  Componente6 = Motor Driver 1A Dual TB6612FNG
  J61 = female pin header, 6 pins [form="♀ (female)"]
  R30 = Resistor [tolerance=±5% resistance=220 package=THT]
  J59 = Screw terminal - 2 pins [package=THT]
  J60 = Screw terminal - 2 pins [package=THT]
  J57 = Screw terminal - 2 pins [package=THT]
  J58 = Screw terminal - 2 pins [package=THT]

nets:
  VCC: R1.pin_0, R3.pin_0, R5.pin_0, R6.pin_0, R8.pin_0, R9.pin_0, R10.pin_0, R11.pin_1, R12.pin_1, R13.pin_1, R14.pin_1, R15.pin_1, RGB_SMD_LED4.DOut, RGB_SMD_LED4.DIn, RGB_SMD_LED4.VCC, RGB_SMD_LED6.DOut, RGB_SMD_LED6.DIn, RGB_SMD_LED6.VCC, RGB_SMD_LED5.NC, RGB_SMD_LED5.VDD, RGB_SMD_LED5.VSS, RGB_SMD_LED1.NC, RGB_SMD_LED1.VDD, RGB_SMD_LED1.VSS, RGB_SMD_LED9.NC, RGB_SMD_LED9.VDD, RGB_SMD_LED9.VSS, RGB_SMD_LED10.NC, RGB_SMD_LED10.VDD, RGB_SMD_LED10.VSS, RGB_SMD_LED7.NC, RGB_SMD_LED7.VDD, RGB_SMD_LED7.VSS, RGB_SMD_LED11.DOut, RGB_SMD_LED11.DIn, RGB_SMD_LED11.VCC, RGB_SMD_LED2.DOut, RGB_SMD_LED2.DIn, RGB_SMD_LED2.VCC, RGB_SMD_LED3.DOut, RGB_SMD_LED3.DIn, RGB_SMD_LED3.VCC, J62.pin1, Componente4.VCC, Componente4.STBY, Componente6.VCC, Componente6.STBY, J61.pin2
  N1: R1.pin_1, R19.Pin_1, U1.GPIO35
  GND: R2.Pin_0, R18.Pin_1, R19.Pin_0, R20.Pin_0, R21.Pin_0, R22.Pin_0, R23.Pin_0, R24.Pin_1, R26.Pin_0, R27.Pin_0, R28.Pin_0, R29.Pin_0, U1.GND, J62.pin2, Componente4.GND, Componente6.GND, J61.pin3, R30.Pin_1
  N2: R2.Pin_1, R3.pin_1, U1.GPIO34
  N3: R5.pin_1, R20.Pin_1, U1.GPIO32
  N4: R6.pin_1, R21.Pin_1, U1.GPIO33
  N5: R8.pin_1, R22.Pin_1, U1.GPIO25
  N6: R9.pin_1, R23.Pin_1, U1.GPIO15
  N7: R10.pin_1, R18.Pin_0, U1.GPIO39
  N8: R11.pin_0, R24.Pin_0, U1.GPIO2
  N9: R12.pin_0, R28.Pin_1, U1.GPIO0
  N10: R13.pin_0, R27.Pin_1, U1.GPIO4
  N11: R14.pin_0, R26.Pin_1
  N12: R15.pin_0, R29.Pin_1, U1.GPIO36
  VDD: RGB_SMD_LED4.NC, RGB_SMD_LED4.VDD, RGB_SMD_LED4.VSS, RGB_SMD_LED6.NC, RGB_SMD_LED6.VDD, RGB_SMD_LED6.VSS, RGB_SMD_LED5.DOut, RGB_SMD_LED5.DIn, RGB_SMD_LED5.VCC, RGB_SMD_LED1.DOut, RGB_SMD_LED1.DIn, RGB_SMD_LED1.VCC, RGB_SMD_LED9.DOut, RGB_SMD_LED9.DIn, RGB_SMD_LED9.VCC, RGB_SMD_LED10.DOut, RGB_SMD_LED10.DIn, RGB_SMD_LED10.VCC, RGB_SMD_LED7.DOut, RGB_SMD_LED7.DIn, RGB_SMD_LED7.VCC, RGB_SMD_LED11.NC, RGB_SMD_LED11.VDD, RGB_SMD_LED11.VSS, RGB_SMD_LED2.NC, RGB_SMD_LED2.VDD, RGB_SMD_LED2.VSS, RGB_SMD_LED3.NC, RGB_SMD_LED3.VDD, RGB_SMD_LED3.VSS, R30.Pin_0
  N13: U1.GPIO14, Componente6.PWMA
  N14: U1.GPIO12, Componente6.AIN2
  N15: U1.GPIO13, Componente6.AIN1
  N16: U1.GPIO9, Componente6.BIN1
  N17: U1.GPIO10, Componente6.BIN2
  N18: U1.VIN, J61.pin4
  N19: U1.GPIO8, Componente6.PWMB
  N20: U1.GPIO16, Componente4.PWMA
  N21: U1.GPIO17, Componente4.AIN1
  N22: U1.GPIO5, Componente4.BIN1
  N23: U1.GPIO18, Componente4.BIN2
  N24: U1.GPIO19, Componente4.PWMB
  N25: U1.GPIO21, J61.pin6
  N26: U1.GPIO22, J61.pin5
  N27: U1.GPIO23, Componente4.AIN2
  N28: Componente4.B01, J57.pin2
  N29: Componente4.B02, J57.pin1
  N30: Componente4.A02, J58.pin2
  N31: Componente4.A01, J58.pin1
  N32: Componente4.VM, Componente6.VM, J61.pin1
  N33: Componente6.B01, J59.pin2
  N34: Componente6.B02, J59.pin1
  N35: Componente6.A02, J60.pin2
  N36: Componente6.A01, J60.pin1

notes:
  VM
  3.3v
  gnd
  SCL
  SDA
  VCC GND
  GREGORIANOS

custom parts:
  ESP32S-HiLetgo: HiLetgo ESP-WROOM-32 ESP32 ESP-32S Development Board 2.4GHz Dual-Mode WiFi + Bluetooth Dual Cores Microcontroller The ESP32 integrated with Antenna switches, RF Balun, power amplifiers, low-noise amplifiers, filters, and management modules, and the entire solution occupies the least area of PCB. 2.4 GHz Wi-Fi plus Bluetooth dual-mode chip, with TSMC Ultra-low power consumption 40nm technology,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
