# Fritzing sketch arriba todo (saved by Fritzing 0.9.3b)
circuit board: 10.5cm x 10.5cm
breadboards: 1

parts:
  Q17 = PNP-Transistor [package="TO92 [THT]"]
  Q18 = PNP-Transistor [package="TO92 [THT]"]
  Q19 = PNP-Transistor [package="TO92 [THT]"]
  Q20 = PNP-Transistor [package="TO92 [THT]"]
  Q21 = PNP-Transistor [package="TO92 [THT]"]
  Q22 = PNP-Transistor [package="TO92 [THT]"]
  Q23 = PNP-Transistor [package="TO92 [THT]"]
  Q24 = PNP-Transistor [package="TO92 [THT]"]
  Q25 = PNP-Transistor [package="TO92 [THT]"]
  Q26 = PNP-Transistor [package="TO92 [THT]"]
  Q27 = PNP-Transistor [package="TO92 [THT]"]
  Q28 = PNP-Transistor [package="TO92 [THT]"]
  Q29 = PNP-Transistor [package="TO92 [THT]"]
  Q30 = PNP-Transistor [package="TO92 [THT]"]
  Q31 = PNP-Transistor [package="TO92 [THT]"]
  Q32 = PNP-Transistor [package="TO92 [THT]"]
  R5 = Resistor [tolerance=±5% resistance=220 package=THT]
  R6 = Resistor [tolerance=±5% resistance=220 package=THT]
  R7 = Resistor [tolerance=±5% resistance=220 package=THT]
  R8 = Resistor [tolerance=±5% resistance=220 package=THT]
  C5 = Ceramic Capacitor [capacitance=100nF package="100 mil [THT, multilayer]"]
  C6 = Ceramic Capacitor [capacitance=100nF package="100 mil [THT, multilayer]"]
  C7 = Ceramic Capacitor [capacitance=100nF package="100 mil [THT, multilayer]"]
  C8 = Ceramic Capacitor [capacitance=100nF package="100 mil [THT, multilayer]"]
  VCC_GND1 = Tilt Switch [package=THT]
  U4 = mystery part, 16 pins [chip_label=?]

nets:
  N1: Q17.E, Q18.E
  N2: Q17.B, Q19.B
  N3: Q17.C, U4.pin14
  N4: Q18.B, Q20.B, Q22.B, Q24.B, Q26.B, Q28.B, Q30.B, Q32.B, C5.1, C6.0, C7.0, C8.1, VCC_GND1.Pin_1
  N5: Q18.C, U4.pin15
  N6: Q19.E, Q24.E, R6.Pin_1, C6.1
  N7: Q19.C, U4.pin16
  N8: Q20.E, Q23.E, R5.Pin_0, C5.0
  N9: Q20.C, U4.pin13
  N10: Q21.E, Q22.E
  N11: Q21.B, Q23.B
  N12: Q21.C, U4.pin12
  N13: Q22.C, U4.pin11
  N14: Q23.C, U4.pin10
  N15: Q24.C, U4.pin2
  N16: Q25.E, Q28.E, R7.Pin_1, C7.1
  N17: Q25.B, Q27.B
  N18: Q25.C, U4.pin1
  N19: Q26.E, Q27.E
  N20: Q26.C, U4.pin3
  N21: Q27.C, U4.pin4
  N22: Q28.C, U4.pin5
  N23: Q29.E, Q32.E, R8.Pin_0, C8.0
  N24: Q29.B, Q31.B
  N25: Q29.C, U4.pin6
  N26: Q30.E, Q31.E
  N27: Q30.C, U4.pin7
  N28: Q31.C, U4.pin8
  N29: Q32.C, U4.pin9
  N30: R5.Pin_1, R6.Pin_0, R7.Pin_0, R8.Pin_1, VCC_GND1.Pin_2

notes:
  GREGORIANOS
